# Fritzing sketch ADS1115 e LM35 (saved by Fritzing 0.9.3b)
breadboards: 1

parts:
  Componente1 = Arduino Nano (Rev3.0) (ICSP)
  Componente2 = Adafruit ADS1115 16Bit I2C ADC [part_number="Adafruit #1085"]
  T1 = LM35 Temperature Sensor [package="TO92 [THT]"]

nets:
  GND: Componente1.GND, Componente2.ADDR, Componente2.GND, T1.GND
  5V: Componente1.5V, Componente2.VDD, T1.+Vs
  N1: Componente1.A5, Componente2.SCL
  N2: Componente1.A4, Componente2.SDA
  N3: Componente2.AIN0, T1.Vout

custom parts:
  Adafruit ADS1115 16Bit I2C ADC: For microcontrollers without an analog-to-digital converter or when you want a higher-precision ADC, the ADS1115 provides 16-bit precision at 860 samples/second over I2C. The chip can be configured as 4 single-ended input channels, or two differential channels. As a nice bonus, it even includes a programmable gain amplifier, up to x16, to help boost up smaller single/differential signals to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
