# Fritzing sketch ads1115 addr (saved by Fritzing 0.9.3b)
breadboards: 1

parts:
  Componente1 = Adafruit ADS1115 16Bit I2C ADC [part_number="Adafruit #1085"]
  Componente2 = Adafruit ADS1115 16Bit I2C ADC [part_number="Adafruit #1085"]
  Componente3 = Adafruit ADS1115 16Bit I2C ADC [part_number="Adafruit #1085"]
  Componente4 = Adafruit ADS1115 16Bit I2C ADC [part_number="Adafruit #1085"]

nets:
  N1: Componente1.ADDR, Componente1.GND
  N2: Componente2.ADDR, Componente2.VDD
  N3: Componente3.ADDR, Componente3.SDA
  N4: Componente4.ADDR, Componente4.SCL

custom parts:
  Adafruit ADS1115 16Bit I2C ADC: For microcontrollers without an analog-to-digital converter or when you want a higher-precision ADC, the ADS1115 provides 16-bit precision at 860 samples/second over I2C. The chip can be configured as 4 single-ended input channels, or two differential channels. As a nice bonus, it even includes a programmable gain amplifier, up to x16, to help boost up smaller single/differential signals to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
